# Fritzing sketch Circuit_Diagram (saved by Fritzing 0.9.0b)
breadboards: 1

parts:
  元件1 = Arduino Uno (Rev3)
  J1 = Basic Servo [part_number=MG995]
  J2 = Basic Servo [part_number=MG995]
  J3 = Basic Servo [part_number=MG995]
  J4 = Basic Servo [part_number=MG995]
  VCC1 = 4 x AAA Battery Mount

nets:
  N1: 元件1.D2, J3.pulse
  N2: 元件1.D3_PWM, J1.pulse
  N3: 元件1.D4, J2.pulse
  N4: 元件1.D5_PWM, J4.pulse
  GND: 元件1.GND, J1.gnd, J2.gnd, J3.gnd, J4.gnd, VCC1.-
  VCC: J1.vcc, J2.vcc, J3.vcc, J4.vcc, VCC1.+
